# Fritzing sketch PhotoresistorWithLED (saved by Fritzing 0.9.3b)
breadboards: 1

parts:
  Componente1 = Arduino Uno (Rev3)
  R1 = PHOTOCELL [package=photocell]
  R2 = Resistor [tolerance=±5% resistance=10k package="0805 [SMD]"]
  LED1 = LED - 5mm [color="Red (633nm)" package="5 mm [THT]"]
  R3 = Resistor [tolerance=±5% resistance=220 package=THT]

nets:
  N1: Componente1.A2, R1.P$2, R2.Pin_0
  N2: Componente1.D9_PWM, R3.Pin_1
  N3: Componente1.5V, R2.Pin_1
  N4: Componente1.GND, R1.P$1, LED1.cathode
  N5: LED1.anode, R3.Pin_0
